# Fritzing sketch circuit_diagram (saved by Fritzing 0.9.3b)

parts:
  Part1 = Adafruit NeoTrellis 4x4 [part_number=https://www.adafruit.com/product/3954]
  Part2 = Arduino Uno (Rev3)

nets:
  VIN: Part1.VIN, Part2.5V
  GND: Part1.GND, Part2.GND
  N1: Part1.SCL, Part2.A5/SCL
  N2: Part1.SDA, Part2.A4/SDA
