# Fritzing sketch lab2_part2_breadboard (saved by Fritzing 0.9.3b)
breadboards: 1

parts:
  Part1 = Arduino Uno (Rev3) - ICSP
  U1 = 74HC595 [package="DIP16 [THT]"]
  U2 = 74HC595 [package="DIP16 [THT]"]
  Dot_Matrix1 = LED Dot Matrix 18mm (0.7 INCH)
  R1 = Resistor [tolerance=±5% resistance=330 package="1206 [SMD]"]
  R2 = Resistor [tolerance=±5% resistance=330 package="1206 [SMD]"]
  R3 = Resistor [tolerance=±5% resistance=330 package="1206 [SMD]"]
  R4 = Resistor [tolerance=±5% resistance=330 package="1206 [SMD]"]
  R5 = Resistor [tolerance=±5% resistance=330 package="1206 [SMD]"]

nets:
  N1: Part1.GND, U1.OE, R1.Pin_1, R2.Pin_1
  N2: Part1.D11_PWM/MOSI, U1.SH_CP, U2.SH_CP
  N3: Part1.D12/MISO, U1.ST_CP, U2.ST_CP
  N4: Part1.D13/SCK, U2.DS
  VCC: Part1.5V, U1.MR, U1.VCC, U2.MR, U2.VCC, R3.Pin_0, R4.Pin_0, R5.Pin_0
  N5: U1.Q1, Dot_Matrix1.Row_4, R2.Pin_0
  N6: U1.Q2, Dot_Matrix1.Row_5, R3.Pin_1
  N7: U1.Q3, Dot_Matrix1.Column_1, R5.Pin_1
  N8: U1.Q4, Dot_Matrix1.Row_3, R4.Pin_1
  N9: U1.DS, U2.Q7'
  N10: U1.Q0, Dot_Matrix1.Column_4, R1.Pin_0
  N11: U2.Q1, Dot_Matrix1.Row_6
  N12: U2.Q2, Dot_Matrix1.Column_5
  N13: U2.Q3, Dot_Matrix1.Column_2
  N14: U2.Q4, Dot_Matrix1.Column_3
  N15: U2.Q5, Dot_Matrix1.Row_2
  N16: U2.Q6, Dot_Matrix1.Row_1
  N17: U2.Q0, Dot_Matrix1.Row_7
