# Fritzing sketch lab2_part1_schematic (saved by Fritzing 0.9.3b)
breadboards: 1

parts:
  Part1 = Arduino Uno (Rev3) - ICSP
  S1 = Pushbutton [package="[SMD]"]

nets:
  N1: Part1.GND, S1.Pin_3, S1.Pin_4
  N2: Part1.D2, S1.Pin_1, S1.Pin_2
