# Fritzing sketch lab2_part2_schematic (saved by Fritzing 0.9.3b)
breadboards: 1

parts:
  Part1 = Arduino Uno (Rev3) - ICSP
  U2 = 74HC595 [package="DIP16 [THT]"]
  Dot_Matrix1 = LED Dot Matrix 18mm (0.7 INCH)  # not connected
  R1 = Resistor [tolerance=±5% resistance=330 package="1206 [SMD]"]
  R2 = Resistor [tolerance=±5% resistance=330 package="1206 [SMD]"]
  R3 = Resistor [tolerance=±5% resistance=330 package="1206 [SMD]"]
  R4 = Resistor [tolerance=±5% resistance=330 package="1206 [SMD]"]
  R5 = Resistor [tolerance=±5% resistance=330 package="1206 [SMD]"]
  U1 = 74HC595 [package="DIP16 [THT]"]

nets (from the breadboard view):
  N1: Part1.GND, U2.OE, R1.Pin_1, R2.Pin_1, R3.Pin_0, R4.Pin_0, R5.Pin_0, U1.OE
  N2: Part1.D11_PWM/MOSI, U2.SH_CP, U1.SH_CP
  N3: Part1.D12/MISO, U2.ST_CP, U1.ST_CP
  N4: Part1.D13/SCK, U2.DS
  VCC: Part1.5V, U2.MR, U2.VCC, U1.MR, U1.VCC
  N5: U2.Q7', U1.DS
  N6: R1.Pin_0, U1.Q0
  N7: R2.Pin_0, U1.Q1
  N8: R3.Pin_1, U1.Q2
  N9: R4.Pin_1, U1.Q4
  N10: R5.Pin_1, U1.Q3
