# Fritzing sketch lab2_part3 (saved by Fritzing 0.9.3b)
breadboards: 1

parts:
  U2 = 74HC595 [package="DIP16 [THT]"]
  R1 = Resistor [tolerance=±5% resistance=330 package="1206 [SMD]"]
  R2 = Resistor [tolerance=±5% resistance=330 package="1206 [SMD]"]
  R3 = Resistor [tolerance=±5% resistance=330 package="1206 [SMD]"]
  R4 = Resistor [tolerance=±5% resistance=330 package="1206 [SMD]"]
  R5 = Resistor [tolerance=±5% resistance=330 package="1206 [SMD]"]
  U1 = 74HC595 [package="DIP16 [THT]"]
  Dot_Matrix1 = LED Dot Matrix 18mm (0.7 INCH)
  Part1 = Arduino Uno (Rev3) - ICSP
  S2 = Pushbutton [package="[SMD]"]

nets:
  N1: U2.Q1, Dot_Matrix1.Row_2
  N2: U2.Q2, Dot_Matrix1.Row_3
  N3: U2.Q3, Dot_Matrix1.Row_4
  N4: U2.Q4, Dot_Matrix1.Row_5
  N5: U2.Q5, Dot_Matrix1.Row_6
  N6: U2.Q6, Dot_Matrix1.Row_7
  N7: U2.Q7', U1.DS
  VCC: U2.MR, U2.VCC, U1.MR, U1.VCC, Part1.5V
  N8: U2.SH_CP, U1.SH_CP, Part1.D11_PWM/MOSI
  N9: U2.ST_CP, U1.ST_CP, Part1.D12/MISO
  N10: U2.OE, R1.Pin_1, R2.Pin_1, R3.Pin_0, R4.Pin_0, R5.Pin_0, U1.OE, Part1.GND, S2.Pin_3, S2.Pin_4
  N11: U2.DS, Part1.D13/SCK
  N12: U2.Q0, Dot_Matrix1.Row_1
  N13: R1.Pin_0, U1.Q0, Dot_Matrix1.Column_1
  N14: R2.Pin_0, U1.Q1, Dot_Matrix1.Column_2
  N15: R3.Pin_1, U1.Q2, Dot_Matrix1.Column_3
  N16: R4.Pin_1, U1.Q3, Dot_Matrix1.Column_4
  N17: R5.Pin_1, U1.Q4, Dot_Matrix1.Column_5
  N18: Part1.D2, S2.Pin_1, S2.Pin_2

// code stored in the sketch: sketch_part2.ino
int digit = 0;
unsigned long time;

char numbers[10][5] = { 
  {0x3E, 0x51, 0x49, 0x45, 0x3E},   // 0
  {0x00, 0x42, 0x7F, 0x40, 0x00},   // 1
  {0x42, 0x61, 0x51, 0x49, 0x46},   // 2
  {0x21, 0x41, 0x45, 0x4B, 0x31},   // 3
  {0x18, 0x14, 0x12, 0x7F, 0x10},   // 4
  {0x27, 0x45, 0x45, 0x45, 0x39},   // 5
  {0x3C, 0x4A, 0x49, 0x49, 0x30},   // 6
  {0x01, 0x71, 0x09, 0x05, 0x03},   // 7
  {0x36, 0x49, 0x49, 0x49, 0x36},   // 8
  {0x06, 0x49, 0x49, 0x29, 0x1E}    // 9
}; 

void setup() {
  // Set latchPin (12) to OUTPUT (1)
  DDRB |= (1 << PB4);

  // Set dataPin (13) to OUTPUT (1)
  DDRB |= (1 << PB5);

  // Set clockPin (11) to OUTPUT (1)
  DDRB |= (1 << PB3);

  // Start timer for cycling through digits
  time = millis();
}

void loop() {
  // Scan through each column and set the rows
  for (int colNum = 0; colNum < 5; colNum++) {
    // Flip the bit for the corresponding column
    char col = B00011111 & ~(1 << colNum);

    // Set latchPin (12) to LOW (0)
    PORTB &= ~(1 << PB4);
    
    writeVal(col);
    writeVal(numbers[digit][colNum]);
    
    // Set latchPin (12) to HIGH (1)
    PORTB |= (1 << PB4);
  }

  // Increment digit after 1 second
  if (millis() > time + 1000) {
    time = millis();
    digit++;

    // Wrap around from 9 back to 0
    if (digit > 9) {
      digit = 0;
    }
  }
}

void writeVal(char value) {
  // Send the data for a row
  for (int i = 7; i >= 0; i--) {
    // Set clockPin (11) to LOW (0)
    PORTB &= ~(1 << PB3);
    
    // Set dataPin (13) to the bit at i in value
    if (value & (1 << i)) {
      PORTB |= (1 << PB5);
    } else {
      PORTB &= ~(1 << PB5);
    }
    
    // Set clockPin (11) to HIGH (1)
    PORTB |= (1 << PB3);
  }
}
