# Fritzing sketch sketch_part1 (saved by Fritzing 0.9.3b)
breadboards: 1

parts:
  Arduino = Arduino Uno (Rev3) - ICSP
  R1 = Resistor [tolerance=±5% resistance=10k package="0805 [SMD]"]
  R2 = PHOTOCELL [package=photocell]

nets:
  N1: Arduino.5V, R2.P$1
  N2: Arduino.GND, R1.Pin_1
  N3: Arduino.D0/RX, R1.Pin_0, R2.P$2
