# Fritzing sketch sketch_part2 (saved by Fritzing 0.9.3b)
breadboards: 1

parts:
  Arduino = Arduino Uno (Rev3) - ICSP
  R1 = Resistor [tolerance=±5% resistance=10k package="0805 [SMD]"]
  R2 = PHOTOCELL [package=photocell]
  hc-sr1 = hc-sr04
  R3 = Resistor [tolerance=±5% resistance=220 package="0402 [SMD]"]
  R4 = Resistor [tolerance=±5% resistance=220 package="0402 [SMD]"]
  R5 = Resistor [tolerance=±5% resistance=220 package="0402 [SMD]"]
  LED1 = RGB LED - (4 legs) [package="5 mm [THT]"]

nets:
  N1: Arduino.A0, R1.Pin_0, R2.P$2
  5V: Arduino.5V, R2.P$1, hc-sr1.VCC, LED1.common_anode
  GND: Arduino.GND, R1.Pin_1, hc-sr1.GND
  N2: Arduino.D9_PWM, R5.Pin_1
  N3: Arduino.D10_PWM/SS, R4.Pin_1
  N4: Arduino.D11_PWM/MOSI, R3.Pin_1
  N5: Arduino.D12/MISO, hc-sr1.Trig
  N6: Arduino.D13/SCK, hc-sr1.Echo
  N7: R3.Pin_0, LED1.red_cathode
  N8: R4.Pin_0, LED1.green_cathode
  N9: R5.Pin_0, LED1.blue_cathode
