# Fritzing sketch sketch_part3_fritzing (saved by Fritzing 0.9.3b)
breadboards: 1

parts:
  part = Arduino Uno (Rev3)
  Rotary_Encoder = Rotary Encoder [package=THT]
  part_2 = 128x64 Monochrom OLED Display with SPI Control

nets:
  N1: part.D8, part_2.Reset
  N2: part.D9_PWM, part_2.SA0/DC
  N3: part.D10_PWM/SS, part_2.CS
  N4: part.D11_PWM/MOSI, part_2.Data
  N5: part.D13/SCK, part_2.Clock
  GND: part.GND, Rotary_Encoder.EncoderPinC, part_2.GND
  N6: part.D2, Rotary_Encoder.EncoderPinB
  N7: part.D3_PWM, Rotary_Encoder.EncoderPinA
  3V3: part.3V3, part_2.3v3
